// Logisim project AyB.circ as structural Verilog: 1 circuit, main circuit main
module main (
  input  A,
  input  B,
  input  A_2,
  input  B_2,
  input  cIn,
  output S,
  output cOut,
  output S_2,
  output cOut_2
);

  wire and_1_out, and_2_out, xor_2_out, xor_3_out;

  and and_1 (and_1_out, B_2, A_2);
  xor xor_1 (cOut_2, cIn, and_1_out);
  and and_2 (and_2_out, B, A);
  xor xor_2 (xor_2_out, A_2, B_2);
  xor xor_3 (xor_3_out, A, B);

  // Notes on the sheet:
  //   Ejercicio A
  //   Ejercicio B
endmodule
