// Logisim project TallerLogica-Combinatorios.circ as structural Verilog: 14 circuits, main circuit sumador_simple
module sumador_simple (
  input  A,
  input  B,
  output S,
  output Cout
);

  xor xor_1 (S, A, B);
  and and_1 (Cout, A, B);
endmodule

module sumador_completo (
  input  A,
  input  B,
  input  Cin,
  output S,
  output Cout
);

  wire sumador_simple_1_cout, sumador_simple_1_s, sumador_simple_2_cout;

  sumador_simple sumador_simple_1 (.A(A), .B(B), .S(sumador_simple_1_s), .Cout(sumador_simple_1_cout));
  sumador_simple sumador_simple_2 (.A(sumador_simple_1_s), .B(Cin), .S(S), .Cout(sumador_simple_2_cout));
  or or_1 (Cout, sumador_simple_2_cout, sumador_simple_1_cout);
endmodule

module sumador_4 (
  input  Cin,
  input  [3:0] A,
  input  [3:0] B,
  output [3:0] S,
  output Cout
);

  wire or_1_out, or_2_out, sumador_completo_1_cout, sumador_completo_2_cout, sumador_completo_3_cout,
       sumador_completo_4_cout;

  sumador_completo sumador_completo_1 (.A(Cin), .B(A[0]), .Cin(B[0]), .S(S[0]), .Cout(sumador_completo_1_cout));
  sumador_completo sumador_completo_2 (
    .A(sumador_completo_1_cout), .B(A[1]), .Cin(B[1]), .S(S[1]), .Cout(sumador_completo_2_cout));
  sumador_completo sumador_completo_3 (
    .A(sumador_completo_2_cout), .B(A[2]), .Cin(B[2]), .S(S[2]), .Cout(sumador_completo_3_cout));
  sumador_completo sumador_completo_4 (
    .A(sumador_completo_3_cout), .B(A[3]), .Cin(B[3]), .S(S[3]), .Cout(sumador_completo_4_cout));
  Hex_Digit_Display hex_digit_display_1 (.value(S));  // open: dp
  or or_1 (or_1_out, sumador_completo_1_cout, sumador_completo_2_cout);
  or or_2 (or_2_out, sumador_completo_3_cout, sumador_completo_4_cout);
  or or_3 (Cout, or_1_out, or_2_out);
endmodule

module comparador_cero (
  input  [3:0] A,
  output Z
);

  wire or_1_out, or_2_out, or_3_out;

  or or_1 (or_1_out, A[0], A[1]);
  or or_2 (or_2_out, A[2], A[3]);
  or or_3 (or_3_out, or_1_out, or_2_out);
  not not_1 (Z, or_3_out);
endmodule

module sumador_flags (
  input  Cin,
  input  [3:0] A,
  input  [3:0] B,
  output [3:0] S,
  output Z,
  output C,
  output N,
  output V
);

  wire not_1_out, xor_1_out, xor_2_out;

  sumador_4 sumador_4_1 (.Cin(Cin), .A(A), .B(B), .S({N, S[2:0]}), .Cout(C));
  Hex_Digit_Display hex_digit_display_1 (.value({N, S[2:0]}));  // open: dp
  xor xor_1 (xor_1_out, N, A[3]);
  xor xor_2 (xor_2_out, A[3], B[3]);
  comparador_cero comparador_cero_1 (.A({N, S[2:0]}), .Z(Z));
  not not_1 (not_1_out, xor_2_out);
  and and_1 (V, xor_1_out, not_1_out);

  assign S[3] = N;
endmodule

module incrementador_4 (
  input  [3:0] A,
  output [3:0] S
);

  sumador_4 sumador_4_1 (.A(4'b0001), .B(A), .S(S));  // open: Cin, Cout
  Hex_Digit_Display hex_digit_display_1 (.value(S));  // open: dp
endmodule

module inversor_4 (
  input  [3:0] A,
  input  INV,
  output [3:0] S
);

  wire [3:0] incrementador_4_1_s, not_1_out;

  assign not_1_out = ~A;  // NOT_Gate not_1, 4 bits wide
  incrementador_4 incrementador_4_1 (.A(not_1_out), .S(incrementador_4_1_s));
  Multiplexer #(.width(4)) multiplexer_1 (.in0(A), .in1(incrementador_4_1_s), .out(S), .sel(INV));
  Hex_Digit_Display #(.decimalPoint("false")) hex_digit_display_1 (.value(S));
endmodule

module Resta (
  input  [3:0] A,
  input  [3:0] B,
  output [3:0] S,
  output V,
  output Bout
);

  wire [3:0] inversor_4_1_s;

  inversor_4 inversor_4_1 (.A(B), .INV(1'b1), .S(inversor_4_1_s));
  sumador_flags sumador_flags_1 (.A(A), .B(inversor_4_1_s), .S(S), .V(V));  // open: Cin, Z, C, N
  hayBorrow hayborrow_1 (.A(A), .B(B), .Bout(Bout));
  Hex_Digit_Display hex_digit_display_1 (.value(S));  // open: dp
endmodule

module AandB (
  input  [3:0] A,
  input  [3:0] B,
  output [3:0] S
);

  and and_1 (S[0], A[0], B[0]);
  and and_2 (S[1], A[1], B[1]);
  and and_3 (S[2], A[2], B[2]);
  and and_4 (S[3], A[3], B[3]);
endmodule

module AorB (
  input  [3:0] A,
  input  [3:0] B,
  output [3:0] S
);

  or or_1 (S[0], A[0], B[0]);
  or or_2 (S[1], A[1], B[1]);
  or or_3 (S[2], A[2], B[2]);
  or or_4 (S[3], A[3], B[3]);
endmodule

module OPvale10o11 (
  input  [1:0] A,
  input  B,
  output S
);

  wire not_1_out;

  not not_1 (not_1_out, A[1]);
  and and_1 (S, not_1_out, B);
endmodule

module ALU (
  input  [3:0] A,
  input  [3:0] B,
  input  [1:0] OP,
  output [3:0] S,
  output Z,
  output C,
  output N,
  output V
);

  wire resta_1_bout, resta_1_v, sumador_flags_1_c, sumador_flags_1_v;
  wire [3:0] aandb_1_s, aorb_1_s, resta_1_s, sumador_flags_1_s;

  sumador_flags sumador_flags_1 (
    .A(A), .B(B), .S(sumador_flags_1_s), .C(sumador_flags_1_c), .V(sumador_flags_1_v));  // open: Cin, Z, N
  Resta resta_1 (.A(A), .B(B), .S(resta_1_s), .V(resta_1_v), .Bout(resta_1_bout));
  AandB aandb_1 (.A(A), .B(B), .S(aandb_1_s));
  AorB aorb_1 (.A(A), .B(B), .S(aorb_1_s));
  Multiplexer #(.select(2), .width(4)) multiplexer_1 (
    .in0(sumador_flags_1_s), .in1(resta_1_s), .in2(aandb_1_s), .in3(aorb_1_s), .out({N, S[2:0]}), .sel(OP));
  Multiplexer #(.select(2)) multiplexer_2 (
    .in0(sumador_flags_1_c), .in1(resta_1_bout), .in2(1'b0), .in3(1'b0), .out(C), .sel(OP));
  Multiplexer #(.select(2)) multiplexer_3 (
    .in0(sumador_flags_1_v), .in1(resta_1_v), .in2(1'b0), .in3(1'b0), .out(V), .sel(OP));
  Hex_Digit_Display hex_digit_display_1 (.value({N, S[2:0]}));  // open: dp
  comparador_cero comparador_cero_1 (.A({N, S[2:0]}), .Z(Z));

  assign S[3] = N;
endmodule

module verificador (
  output [3:0] out_1,
  output [3:0] out_2,
  output [1:0] out_3,
  output halt,
  output N,
  output Z,
  output V,
  output C,
  output [3:0] res
);

  wire clock_1_out;

  Clock clock_1 (.out(clock_1_out));
  Counter #(.max('h3ff), .width(10)) counter_1 (
    .clk(clock_1_out), .carry(halt), .Q({out_3, out_2, out_1}));  // open: clr, load, up, count, D
  // ALU alu_1: pin names not known; wires that end beside it: out_1, out_2, out_3, N, Z, V, C, res
endmodule

module hayBorrow (
  input  [3:0] A,
  input  [3:0] B,
  output Bout
);

  wire and_1_out, and_2_out, and_3_out, and_4_out, or_1_out, or_2_out;
  wire [3:0] not_1_out;

  assign not_1_out = ~A;  // NOT_Gate not_1, 4 bits wide
  and and_1 (and_1_out, not_1_out[0], B[0]);
  and and_2 (and_2_out, not_1_out[1], B[1]);
  and and_3 (and_3_out, not_1_out[3], B[3]);
  and and_4 (and_4_out, not_1_out[2], B[2]);
  or or_1 (or_1_out, and_1_out, and_2_out);
  or or_2 (or_2_out, and_4_out, and_3_out);
  or or_3 (Bout, or_1_out, or_2_out);
endmodule
